# Fritzing sketch MotorTest (saved by Fritzing 0.9.3b)
circuit board: 8.46667cm x 5.64444cm
breadboards: 1

parts:
  DPDT_Relay2 = DPDT Relay [chip_label=Relay package="DIP (Dual Inline) [THT]"]
  DPDT_Relay4 = DPDT Relay [chip_label=Relay package="DIP (Dual Inline) [THT]"]
  DPDT_Relay5 = DPDT Relay [chip_label=Relay package="DIP (Dual Inline) [THT]"]
  DPDT_Relay6 = DPDT Relay [chip_label=Relay package="DIP (Dual Inline) [THT]"]
  J1 = female pin header, 1 pin [form="♀ (female)"]
  J2 = female pin header, 1 pin [form="♀ (female)"]
  J3 = female pin header, 1 pin [form="♀ (female)"]
  J4 = female pin header, 1 pin [form="♀ (female)"]
  J5 = female pin header, 1 pin [form="♀ (female)"]
  J7 = female pin header, 1 pin [form="♀ (female)"]
  J8 = female pin header, 1 pin [form="♀ (female)"]
  J9 = female pin header, 1 pin [form="♀ (female)"]
  J10 = female pin header, 1 pin [form="♀ (female)"]
  J11 = female pin header, 1 pin [form="♀ (female)"]
  J12 = female pin header, 1 pin [form="♀ (female)"]
  J13 = female pin header, 1 pin [form="♀ (female)"]
  J14 = female pin header, 1 pin [form="♀ (female)"]
  DPDT_Relay1 = DPDT Relay [chip_label=Relay package="DIP (Dual Inline) [THT]"]
  D1 = Rectifier Diode [part_number=1N4001 package="300 mil [THT]"]
  D2 = Rectifier Diode [part_number=1N4001 package="300 mil [THT]"]
  D3 = Rectifier Diode [part_number=1N4001 package="300 mil [THT]"]
  D4 = Rectifier Diode [part_number=1N4001 package="300 mil [THT]"]
  D5 = Rectifier Diode [part_number=1N4001 package="300 mil [THT]"]
  D6 = Rectifier Diode [part_number=1N4001 package="300 mil [THT]"]
  Q1 = NPN-Transistor [package="TO92 [THT]"]
  R1 = Resistor [tolerance=±5% resistance=10k package=THT]
  Q2 = NPN-Transistor [package="TO92 [THT]"]
  Q3 = NPN-Transistor [package="TO92 [THT]"]
  Q4 = NPN-Transistor [package="TO92 [THT]"]
  Q5 = NPN-Transistor [package="TO92 [THT]"]
  Q6 = NPN-Transistor [package="TO92 [THT]"]
  R2 = Resistor [tolerance=±5% resistance=10k package=THT]
  R3 = Resistor [tolerance=±5% resistance=10k package=THT]
  R4 = Resistor [tolerance=±5% resistance=10k package=THT]
  R5 = Resistor [tolerance=±5% resistance=10k package=THT]
  R6 = Resistor [tolerance=±5% resistance=10k package=THT]
  DPDT_Relay3 = DPDT Relay [chip_label=Relay package="DIP (Dual Inline) [THT]"]
  J6 = female pin header, 1 pin [form="♀ (female)"]
  J15 = female pin header, 1 pin [form="♀ (female)"]
  J16 = female pin header, 1 pin [form="♀ (female)"]
  R7 = Resistor [tolerance=±5% resistance=1k package=THT]
  J17 = female pin header, 1 pin [form="♀ (female)"]
  R8 = Resistor [tolerance=±5% resistance=1k package=THT]
  J18 = female pin header, 1 pin [form="♀ (female)"]
  J19 = female pin header, 1 pin [form="♀ (female)"]
  J20 = female pin header, 1 pin [form="♀ (female)"]
  J21 = female pin header, 1 pin [form="♀ (female)"]
  J22 = female pin header, 1 pin [form="♀ (female)"]
  J23 = female pin header, 1 pin [form="♀ (female)"]
  J24 = female pin header, 1 pin [form="♀ (female)"]
  J25 = female pin header, 1 pin [form="♀ (female)"]
  J26 = female pin header, 1 pin [form="♀ (female)"]
  J27 = female pin header, 1 pin [form="♀ (female)"]
  J28 = female pin header, 1 pin [form="♀ (female)"]
  J29 = female pin header, 1 pin [form="♀ (female)"]
  R9 = Resistor [tolerance=±5% resistance=1k package=THT]
  R10 = Resistor [tolerance=±5% resistance=1k package=THT]
  R11 = Resistor [tolerance=±5% resistance=1k package=THT]
  R12 = Resistor [tolerance=±5% resistance=1k package=THT]
  R13 = Resistor [tolerance=±5% resistance=1k package=THT]
  R14 = Resistor [tolerance=±5% resistance=1k package=THT]
  R15 = Resistor [tolerance=±5% resistance=1k package=THT]
  R16 = Resistor [tolerance=±5% resistance=1k package=THT]
  DPDT_Relay7 = DPDT Relay [chip_label=Relay package="DIP (Dual Inline) [THT]"]
  Q8 = PNP-Transistor [package="TO92 [THT]"]
  R17 = Resistor [tolerance=±5% resistance=10k package=THT]
  Q10 = NPN-Transistor [package="TO92 [THT]"]
  R18 = Resistor [tolerance=±5% resistance=10k package=THT]
  R19 = Resistor [tolerance=±5% resistance=10k package=THT]
  IN = female pin header, 1 pin [form="♀ (female)"]
  Out = female pin header, 1 pin [form="♀ (female)"]
  IN1 = female pin header, 1 pin [form="♀ (female)"]
  IN2 = female pin header, 1 pin [form="♀ (female)"]
  Q11 = PNP-Transistor [package="TO92 [THT]"]
  Q12 = NPN-Transistor [package="TO92 [THT]"]
  R20 = Resistor [tolerance=±5% resistance=10k package=THT]
  R21 = Resistor [tolerance=±5% resistance=10k package=THT]
  R22 = Resistor [tolerance=±5% resistance=10k package=THT]
  IN3 = female pin header, 1 pin [form="♀ (female)"]
  IN4 = female pin header, 1 pin [form="♀ (female)"]
  Out1 = female pin header, 1 pin [form="♀ (female)"]
  IN5 = female pin header, 1 pin [form="♀ (female)"]
  D7 = Rectifier Diode [part_number=1N4001 package="300 mil [THT]"]
  Q13 = NPN-Transistor [package="TO92 [THT]"]
  R23 = Resistor [tolerance=±5% resistance=10k package=THT]
  Out2 = female pin header, 1 pin [form="♀ (female)"]
  DPDT_Relay8 = DPDT Relay [chip_label=Relay package="DIP (Dual Inline) [THT]"]
  IN6 = female pin header, 1 pin [form="♀ (female)"]
  IN7 = female pin header, 1 pin [form="♀ (female)"]
  IN8 = female pin header, 1 pin [form="♀ (female)"]
  Out3 = female pin header, 1 pin [form="♀ (female)"]
  Out4 = female pin header, 1 pin [form="♀ (female)"]
  IN9 = female pin header, 1 pin [form="♀ (female)"]
  IN10 = female pin header, 1 pin [form="♀ (female)"]
  IN11 = female pin header, 1 pin [form="♀ (female)"]
  Out5 = female pin header, 1 pin [form="♀ (female)"]
  D8 = Rectifier Diode [part_number=1N4001 package="300 mil [THT]"]
  Q14 = NPN-Transistor [package="TO92 [THT]"]
  R24 = Resistor [tolerance=±5% resistance=10k package=THT]
  R25 = Resistor [tolerance=±5% resistance=10k package=THT]
  R26 = Resistor [tolerance=±5% resistance=10k package=THT]
  R27 = Resistor [tolerance=±5% resistance=10k package=THT]
  R28 = Resistor [tolerance=±5% resistance=10k package=THT]
  R29 = Resistor [tolerance=±5% resistance=10k package=THT]
  R30 = Resistor [tolerance=±5% resistance=10k package=THT]
  Q15 = PNP-Transistor [package="TO92 [THT]"]
  Q16 = PNP-Transistor [package="TO92 [THT]"]
  Q17 = NPN-Transistor [package="TO92 [THT]"]
  Q18 = NPN-Transistor [package="TO92 [THT]"]
  DPDT_Relay9 = DPDT Relay [chip_label=Relay package="DIP (Dual Inline) [THT]"]
  IN13 = female pin header, 1 pin [form="♀ (female)"]
  IN14 = female pin header, 1 pin [form="♀ (female)"]
  Out6 = female pin header, 1 pin [form="♀ (female)"]
  Out7 = female pin header, 1 pin [form="♀ (female)"]
  IN15 = female pin header, 1 pin [form="♀ (female)"]
  D9 = Rectifier Diode [part_number=1N4001 package="300 mil [THT]"]
  Q19 = NPN-Transistor [package="TO92 [THT]"]
  R32 = Resistor [tolerance=±5% resistance=10k package=THT]
  R33 = Resistor [tolerance=±5% resistance=10k package=THT]
  R34 = Resistor [tolerance=±5% resistance=10k package=THT]
  R37 = Resistor [tolerance=±5% resistance=10k package=THT]
  Q21 = PNP-Transistor [package="TO92 [THT]"]
  Q22 = NPN-Transistor [package="TO92 [THT]"]
  5V = female pin header, 1 pin [form="♀ (female)"]
  12v = female pin header, 1 pin [form="♀ (female)"]
  GND = female pin header, 1 pin [form="♀ (female)"]

nets:
  N1: DPDT_Relay2.pin1, DPDT_Relay4.pin1, DPDT_Relay5.pin1, DPDT_Relay6.pin1, DPDT_Relay1.pin1, D1.cathode, D2.cathode, D3.cathode, D4.cathode, D5.cathode, D6.cathode, DPDT_Relay3.pin1, J15.pin1
  N2: DPDT_Relay2.pin5, DPDT_Relay4.pin5, DPDT_Relay5.pin5, J14.pin1, DPDT_Relay1.pin5, DPDT_Relay3.pin5
  N3: DPDT_Relay2.pin6, DPDT_Relay4.pin6, DPDT_Relay5.pin6, DPDT_Relay6.pin5, DPDT_Relay1.pin6, DPDT_Relay3.pin6
  N4: DPDT_Relay2.pin7, J2.pin1, J26.pin1
  N5: DPDT_Relay2.pin8, D2.anode, Q2.C
  N6: DPDT_Relay4.pin7, J4.pin1, J20.pin1
  N7: DPDT_Relay4.pin8, D5.anode, Q4.C
  N8: DPDT_Relay5.pin7, J5.pin1, J16.pin1, R7.Pin_1, J17.pin1
  N9: DPDT_Relay5.pin8, D4.anode, Q5.C
  N10: DPDT_Relay6.pin7, J13.pin1, Q1.E, Q2.E, Q3.E, Q4.E, Q5.E, Q6.E, R8.Pin_0, R9.Pin_0, R11.Pin_0, R13.Pin_0, R15.Pin_0
  N11: DPDT_Relay6.pin8, D6.anode, Q6.C
  N12: J1.pin1, DPDT_Relay1.pin7, J29.pin1
  N13: J3.pin1, DPDT_Relay3.pin7, J23.pin1
  N14: J7.pin1, R2.Pin_0
  N15: J8.pin1, R1.Pin_0
  N16: J9.pin1, R3.Pin_0
  N17: J10.pin1, R4.Pin_0
  N18: J11.pin1, R5.Pin_0
  N19: J12.pin1, R6.Pin_0
  N20: DPDT_Relay1.pin8, D1.anode, Q1.C
  N21: D3.anode, Q3.C, DPDT_Relay3.pin8
  N22: Q1.B, R1.Pin_1
  N23: Q2.B, R2.Pin_1
  N24: Q3.B, R3.Pin_1
  N25: Q4.B, R4.Pin_1
  N26: Q5.B, R5.Pin_1
  N27: Q6.B, R6.Pin_1
  N28: J6.pin1, R7.Pin_0, R8.Pin_1
  N29: J18.pin1, R9.Pin_1, R10.Pin_0
  N30: J19.pin1, R10.Pin_1
  N31: J21.pin1, R11.Pin_1, R12.Pin_0
  N32: J22.pin1, R12.Pin_1
  N33: J24.pin1, R13.Pin_1, R14.Pin_0
  N34: J25.pin1, R14.Pin_1
  N35: J27.pin1, R15.Pin_1, R16.Pin_0
  N36: J28.pin1, R16.Pin_1
  N37: DPDT_Relay7.pin1, D7.cathode, DPDT_Relay8.pin1, D8.cathode, DPDT_Relay9.pin1, D9.cathode, 5V.pin1
  N38: DPDT_Relay7.pin2, Out.pin1
  N39: DPDT_Relay7.pin3, IN.pin1
  N40: DPDT_Relay7.pin4, Q8.C, Q10.C
  N41: DPDT_Relay7.pin5, Q11.C, Q12.C
  N42: DPDT_Relay7.pin6, IN5.pin1
  N43: DPDT_Relay7.pin7, Out1.pin1
  N44: DPDT_Relay7.pin8, D7.anode, Q13.C
  N45: Q8.E, R18.Pin_1, Q11.E, R21.Pin_1, R25.Pin_1, R30.Pin_1, Q15.E, Q16.E, R33.Pin_1, Q21.E, 12v.pin1
  N46: Q8.B, R17.Pin_0, R18.Pin_0
  N47: R17.Pin_1, IN1.pin1
  N48: Q10.E, Q12.E, Q13.E, Q14.E, Q17.E, Q18.E, Q19.E, GND.pin1
  N49: Q10.B, R19.Pin_0
  N50: R19.Pin_1, IN2.pin1
  N51: Q11.B, R20.Pin_0, R21.Pin_0
  N52: Q12.B, R22.Pin_0
  N53: R20.Pin_1, IN3.pin1
  N54: R22.Pin_1, IN4.pin1
  N55: Q13.B, R23.Pin_0
  N56: R23.Pin_1, Out2.pin1
  N57: DPDT_Relay8.pin2, Out4.pin1
  N58: DPDT_Relay8.pin3, IN9.pin1
  N59: DPDT_Relay8.pin4, Q15.C, Q17.C
  N60: DPDT_Relay8.pin5, Q16.C, Q18.C
  N61: DPDT_Relay8.pin6, IN7.pin1
  N62: DPDT_Relay8.pin7, Out3.pin1
  N63: DPDT_Relay8.pin8, D8.anode, Q14.C
  N64: IN6.pin1, R27.Pin_1
  N65: IN8.pin1, R29.Pin_1
  N66: IN10.pin1, R28.Pin_1
  N67: IN11.pin1, R26.Pin_1
  N68: Out5.pin1, R24.Pin_1
  N69: Q14.B, R24.Pin_0
  N70: R25.Pin_0, R27.Pin_0, Q15.B
  N71: R26.Pin_0, Q18.B
  N72: R28.Pin_0, Q17.B
  N73: R29.Pin_0, R30.Pin_0, Q16.B
  N74: DPDT_Relay9.pin2, Out7.pin1
  N75: DPDT_Relay9.pin3, IN14.pin1
  N76: DPDT_Relay9.pin4, Q21.C, Q22.C
  N77: DPDT_Relay9.pin8, D9.anode, Q19.C
  N78: IN13.pin1, R34.Pin_1
  N79: Out6.pin1, R37.Pin_1
  N80: IN15.pin1, R32.Pin_1
  N81: Q19.B, R37.Pin_0
  N82: R32.Pin_0, R33.Pin_0, Q21.B
  N83: R34.Pin_0, Q22.B

custom parts:
  DPDT Relay: DIP DPDT Relay (Double Pole Double Throw)
